# Fritzing sketch motionProt (saved by Fritzing 0.9.10b)

parts:
  Part2 = Arduino Uno (Rev3) - ICSP
  J11 = Basic Servo
  J12 = Basic Servo
  J13 = Basic Servo
  J14 = Basic Servo
  J15 = Basic Servo
  J16 = Basic Servo
  Part3 = InvenSense MPU6050
  Power_plug1 = Power plug  # not connected

nets:
  N1: Part2.A4/SDA, Part3.SDA
  N2: Part2.A5/SCL, Part3.SCL
  N3: Part2.D9_PWM, J13.pulse
  N4: Part2.D10_PWM/SS, J14.pulse
  N5: Part2.D11_PWM/MOSI, J11.pulse
  N6: Part2.D3_PWM, J16.pulse
  N7: Part2.D5_PWM, J15.pulse
  N8: Part2.D6_PWM, J12.pulse
  5V: Part2.5V, Part3.VCC
  GND: Part2.GND, Part3.GND
  GND_2: J11.gnd, J12.gnd, J13.gnd, J14.gnd
  VCC: J12.vcc, J13.vcc, J14.vcc, J15.vcc
  GND_3: J15.gnd, J16.gnd

notes:
  5V 5A power adapter stripped to attach 6 jumper wires and a ground wire. All servo power and ground wires are common
  Using laptop to power the Arduino
