# Fritzing sketch ver1 (saved by Fritzing 0.9.10b)
breadboards: 1

parts:
  J3 = Basic Servo
  J4 = Basic Servo
  J6 = Basic Servo
  Part1 = Arduino Uno (Rev3) - ICSP
  J7 = Basic Servo
  J8 = Basic Servo
  J9 = Basic Servo

nets:
  GND: J3.gnd, J4.gnd, J6.gnd, Part1.GND
  VCC: J3.vcc, J4.vcc, J6.vcc, Part1.5V
  N1: J3.pulse, Part1.D5_PWM
  N2: J4.pulse, Part1.D6_PWM
  N3: J6.pulse, Part1.D3_PWM
  N4: Part1.D9_PWM, J9.pulse
  N5: Part1.D10_PWM/SS, J8.pulse
  N6: Part1.D11_PWM/MOSI, J7.pulse
  GND_2: J7.gnd, J8.gnd, J9.gnd
  VCC_2: J7.vcc, J8.vcc, J9.vcc

notes:
  Using a 7V 1A adapter to power Arduino
