# Fritzing sketch ver2 (saved by Fritzing 0.9.10b)
breadboards: 1

parts:
  Part2 = Arduino Uno (Rev3) - ICSP
  J14 = Basic Servo
  PWM1 = PCA9685 16x12-bit PWM Breakout
  J15 = Basic Servo
  J16 = Basic Servo
  J18 = Basic Servo
  J19 = Basic Servo
  J20 = Basic Servo
  PSU1 = Adjustable Breadboard Power Supply
  Power_plug3 = Power plug

nets:
  N1: Part2.A4/SDA, PWM1.no_name_yet#504
  N2: Part2.A5/SCL, PWM1.no_name_yet#503
  N3: Part2.5V, PWM1.no_name_yet#505
  N4: Part2.GND, PWM1.no_name_yet#501, PWM1.no_name_yet#701, PWM1.no_name_yet#1000, PWM1.no_name_yet#1001, PWM1.no_name_yet#1002, PWM1.no_name_yet#1004, PWM1.no_name_yet#1005, PWM1.no_name_yet#1006
  N5: J14.pulse, PWM1.no_name_yet#0
  N6: PWM1.no_name_yet#1, J15.pulse
  N7: PWM1.no_name_yet#2, J16.pulse
  N8: PWM1.no_name_yet#4, J18.pulse
  N9: PWM1.no_name_yet#5, J19.pulse
  N10: PWM1.no_name_yet#6, J20.pulse
  N11: PWM1.no_name_yet#100, PWM1.no_name_yet#101, PWM1.no_name_yet#102, PWM1.no_name_yet#104, PWM1.no_name_yet#105, PWM1.no_name_yet#106, PWM1.no_name_yet#706
  N12: PSU1.Vin2+, Power_plug3.GND
  N13: PSU1.Vin2-, Power_plug3.VCC

notes:
  7.5V 2A battery
  Using laptop to power the Arduino
