# Fritzing sketch ver3 (saved by Fritzing 0.9.10b)

parts:
  J5 = Basic Servo
  J6 = Basic Servo
  J7 = Basic Servo
  J8 = Basic Servo
  J9 = Basic Servo
  J10 = Basic Servo
  Part1 = Arduino Uno (Rev3) - ICSP
  Power_plug2 = Power plug  # not connected

nets:
  GND: J5.gnd, J6.gnd, J7.gnd, J8.gnd
  N1: J5.pulse, Part1.D11_PWM/MOSI
  VCC: J6.vcc, J7.vcc, J8.vcc, J10.vcc
  N2: J6.pulse, Part1.D10_PWM/SS
  N3: J7.pulse, Part1.D9_PWM
  N4: J8.pulse, Part1.D6_PWM
  GND_2: J9.gnd, J10.gnd
  N5: J9.pulse, Part1.D3_PWM
  N6: J10.pulse, Part1.D5_PWM

notes:
  5V 5A power adapter stripped to attach 6 jumper wires and a ground wire. All servo power and ground wires are common
  Using laptop to power the Arduino
